# Fritzing sketch прототип1 (saved by Fritzing 0.9.3b)
breadboards: 2

parts:
  S1 = Pushbutton [package="[THT]"]
  Часть2 = LED Matrix - Serial Interface - Red/Green/Blue
  J1 = Piezo Speaker
  Q1 = NPN-Transistor [package="TO92 [THT]"]
  Часть3 = TM1637

nets:
  N1: S1.Pin_1, S1.Pin_2
  N2: S1.Pin_3, S1.Pin_4, J1.pin1
  N3: Часть2.SCK, Часть3.GND
  VCC: Часть2.VCC, Часть3.VCC
  N4: J1.pin2, Q1.E

custom parts:
  TM1637: A 4 7-seg display
